# Fritzing sketch Wav player (saved by Fritzing 0.9.2b)
breadboards: 1

parts:
  Part1 = Arduino Nano (Rev3.0)
  SD_card_module1 = SD Card Module
  S1 = Pushbutton [package="[THT]"]
  S2 = Pushbutton [package="[THT]"]
  S3 = Pushbutton [package="[THT]"]
  S4 = Pushbutton [package="[THT]"]
  R7 = Resistor [tolerance=±5% resistance=22k package=THT]
  R5 = Resistor [tolerance=±5% resistance=22k package=THT]
  R6 = Resistor [tolerance=±5% resistance=22k package=THT]
  R8 = Resistor [tolerance=±5% resistance=22k package=THT]
  BC546b = NPN-Transistor [package="TO92 [THT]"]
  SPKR1 = Loudspeaker
  R9 = Resistor [tolerance=±5% resistance=4.7k package=THT]
  part = Resistor [tolerance=±5% resistance=220 package=THT]  # not connected

nets:
  N1: Part1.GND, SD_card_module1.GND#0
  N2: Part1.D4, SD_card_module1.CS
  N3: Part1.D9, R9.Pin_0
  N4: Part1.D11/MOSI, SD_card_module1.MOSI
  N5: Part1.D12/MISO, SD_card_module1.MISO
  N6: Part1.5V, SD_card_module1.+5
  N7: Part1.A3, S1.Pin_3, S1.Pin_4, R7.Pin_0
  N8: Part1.A2, S2.Pin_3, S2.Pin_4, R5.Pin_0
  N9: Part1.A1, S3.Pin_3, S3.Pin_4, R6.Pin_0
  N10: Part1.A0, SD_card_module1.GND#7, S4.Pin_1, S4.Pin_2, R8.Pin_0, BC546b.E
  N11: Part1.D13/SCK, SD_card_module1.SCK
  N12: S1.Pin_1, S1.Pin_2
  N13: S2.Pin_1, S2.Pin_2
  N14: S3.Pin_1, S3.Pin_2
  N15: S4.Pin_3, S4.Pin_4
  N16: R7.Pin_1, R5.Pin_1, R6.Pin_1, R8.Pin_1, SPKR1.pin2
  N17: BC546b.B, R9.Pin_1
  N18: BC546b.C, SPKR1.pin1

custom parts:
  SD Card Module: SD Card Module Slot Socket Reader For Arduino ARM MCU
